// Logisim project FCSD.circ as structural Verilog
module main (
  input  [7:0] Manual_Address_Innput,
  input  Load,
  input  Clear,
  input  Carry_In,
  output [7:0] Address_out,
  output [1:0] OpCode,
  output [3:0] Op_A,
  output Flag,
  output [3:0] Op_B,
  output [1:0] out_10,
  output [1:0] Op_Code,
  output [3:0] Output,
  output [1:0] Address_A,
  output [1:0] Data_Address,
  output [1:0] Address_B
);

  wire adder_2_cout, and_1_out, and_2_out, and_3_out, and_4_out, clock_1_out, clock_2_out, clock_3_out,
       decoder_1_out0, decoder_1_out1, decoder_1_out2, decoder_1_out3, multiplexer_10_out, subtractor_1_bout;
  wire [1:0] multiplexer_1_out;
  wire [3:0] adder_2_out, and_5_out, multiplexer_7_out, or_1_out, ram_1_data, register_2_q, register_3_q,
       register_4_q, register_5_q, subtractor_1_out;
  wire [7:0] adder_1_out, multiplexer_5_out, multiplexer_6_out;

  Register #(.width(4)) IR (.D(ram_1_data), .Q({Op_Code, OpCode}), .clk(clock_1_out), .clr(1'b0));  // open: en
  Clock clock_1 (.out(clock_1_out));
  RAM #(.dataWidth(4)) ram_1 (.addr(Address_out), .data(ram_1_data));  // open: sel, clk, ld, clr
  Multiplexer #(.select(2), .width(2), .enable("false")) multiplexer_1 (
    .in0(2'b11), .in1(2'b00), .in2(2'b00), .in3(2'b00), .out(multiplexer_1_out), .sel(OpCode));
  Multiplexer #(.select(2), .width(2), .enable("false")) multiplexer_2 (
    .in0(2'b00), .in1(OpCode), .in2(Address_A), .in3(OpCode), .out(Address_A), .sel(Op_Code));
  Multiplexer #(.select(2), .width(2), .enable("false")) multiplexer_3 (
    .in0(2'b11), .in1(OpCode), .in2(Address_B), .in3(OpCode), .out(Address_B), .sel(Op_Code));
  Multiplexer #(.select(2), .width(2), .enable("false")) multiplexer_4 (
    .in0(2'b00), .in1(multiplexer_1_out), .in2(2'b10), .in3(OpCode), .out(Data_Address), .sel(Op_Code));
  Decoder #(.select(2), .enable("false")) decoder_1 (
    .out0(decoder_1_out0), .out1(decoder_1_out1), .out2(decoder_1_out2), .out3(decoder_1_out3),
    .sel(Data_Address));
  Multiplexer #(.width(8), .enable("false")) multiplexer_5 (
    .in0(adder_1_out), .in1(Manual_Address_Innput), .out(multiplexer_5_out), .sel(Load));
  Clock clock_2 (.out(clock_2_out));
  Multiplexer #(.width(8), .enable("false")) multiplexer_6 (
    .in0(8'h1), .in1({8{1'b0}}), .out(multiplexer_6_out), .sel(Load));
  Multiplexer #(.select(2), .width(4), .enable("false")) multiplexer_7 (
    .in0(Output), .in1(Op_B), .in2({2'b00, OpCode}), .out(multiplexer_7_out), .sel(Op_Code));  // open: in3
  Register register_1 (.D(multiplexer_5_out), .Q(Address_out), .clk(clock_2_out), .clr(Clear));  // open: en
  and and_1 (and_1_out, decoder_1_out0, 1'b1);
  and and_2 (and_2_out, decoder_1_out1, 1'b1);
  and and_3 (and_3_out, decoder_1_out2, 1'b1);
  and and_4 (and_4_out, decoder_1_out3, 1'b1);
  Register #(.width(4)) register_2 (
    .D(multiplexer_7_out), .en(and_1_out), .Q(register_2_q), .clk(clock_3_out), .clr(1'b0));
  Register #(.width(4)) register_3 (
    .D(multiplexer_7_out), .en(and_2_out), .Q(register_3_q), .clk(clock_3_out), .clr(1'b0));
  Register #(.width(4)) register_4 (
    .D(multiplexer_7_out), .en(and_3_out), .Q(register_4_q), .clk(clock_3_out), .clr(1'b0));
  Register #(.width(4)) register_5 (
    .D(multiplexer_7_out), .en(and_4_out), .Q(register_5_q), .clk(clock_3_out), .clr(1'b0));
  Clock clock_3 (.out(clock_3_out));
  Adder adder_1 (.a(Address_out), .b(multiplexer_6_out), .out(adder_1_out), .cin(1'b0), .cout(Clear));
  Multiplexer #(.select(2), .width(4), .enable("false")) multiplexer_8 (
    .in0(register_2_q), .in1(register_3_q), .in2(register_4_q), .in3(register_5_q), .out(Op_A),
    .sel(Address_A));
  Multiplexer #(.select(2), .width(4), .enable("false")) multiplexer_9 (
    .in0(register_2_q), .in1(register_3_q), .in2(register_4_q), .in3(register_5_q), .out(Op_B),
    .sel(Address_B));
  Adder #(.width(4)) adder_2 (.a(Op_A), .b(Op_B), .out(adder_2_out), .cin(Carry_In), .cout(adder_2_cout));
  Subtractor #(.width(4)) subtractor_1 (
    .a(Op_A), .b(Op_B), .out(subtractor_1_out), .bin(Carry_In), .bout(subtractor_1_bout));
  assign and_5_out = Op_A & Op_B;  // AND_Gate and_5, 4 bits wide
  assign or_1_out = Op_A | Op_B;  // OR_Gate or_1, 4 bits wide
  Multiplexer #(.select(2), .enable("false")) multiplexer_10 (
    .in0(adder_2_cout), .in1(subtractor_1_bout), .in2(1'b0), .in3(1'b0), .out(multiplexer_10_out),
    .sel(OpCode));
  Multiplexer #(.select(2), .width(4), .enable("false")) multiplexer_11 (
    .in0(adder_2_out), .in1(subtractor_1_out), .in2(and_5_out), .in3(or_1_out), .out(Output), .sel(OpCode));
  Register #(.width(1)) PSW (.D(multiplexer_10_out), .Q(Flag));  // open: en, clk, clr

  assign out_10 = OpCode;

  // Notes on the sheet:
  //   Load
endmodule

module Registers (
  input  [3:0] ALU,
  input  [1:0] in_2,
  input  [1:0] Op_Code,
  input  [3:0] RAM,
  input  Load,
  input  [1:0] Address_A,
  input  [1:0] Data_Address,
  input  [1:0] Address_B,
  output [3:0] Operator_A,
  output [3:0] Operator_B
);

  wire and_1_out, and_2_out, and_3_out, and_4_out, clock_1_out, decoder_1_out0, decoder_1_out1,
       decoder_1_out2, decoder_1_out3;
  wire [3:0] multiplexer_1_out, register_1_q, register_2_q, register_3_q, register_4_q;

  Hex_Digit_Display hex_digit_display_1 (.value({in_2, 2'b00}), .dp(1'b0));
  Decoder #(.select(2), .enable("false")) decoder_1 (
    .out0(decoder_1_out0), .out1(decoder_1_out1), .out2(decoder_1_out2), .out3(decoder_1_out3),
    .sel(Data_Address));
  Multiplexer #(.select(2), .width(4), .enable("false")) multiplexer_1 (
    .in0(ALU), .in1(Operator_B), .in2({in_2, 2'b00}), .in3(RAM), .out(multiplexer_1_out), .sel(Op_Code));
  and and_1 (and_1_out, decoder_1_out0, Load);
  and and_2 (and_2_out, decoder_1_out1, Load);
  and and_3 (and_3_out, decoder_1_out2, Load);
  and and_4 (and_4_out, decoder_1_out3, Load);
  Register #(.width(4)) register_1 (
    .D(multiplexer_1_out), .en(and_1_out), .Q(register_1_q), .clk(clock_1_out), .clr(1'b0));
  Register #(.width(4)) register_2 (
    .D(multiplexer_1_out), .en(and_2_out), .Q(register_2_q), .clk(clock_1_out), .clr(1'b0));
  Register #(.width(4)) register_3 (
    .D(multiplexer_1_out), .en(and_3_out), .Q(register_3_q), .clk(clock_1_out), .clr(1'b0));
  Register #(.width(4)) register_4 (
    .D(multiplexer_1_out), .en(and_4_out), .Q(register_4_q), .clk(clock_1_out), .clr(1'b0));
  Clock clock_1 (.out(clock_1_out));
  Multiplexer #(.select(2), .width(4), .enable("false")) multiplexer_2 (
    .in0(register_1_q), .in1(register_2_q), .in2(register_3_q), .in3(register_4_q), .out(Operator_A),
    .sel(Address_A));
  Multiplexer #(.select(2), .width(4), .enable("false")) multiplexer_3 (
    .in0(register_1_q), .in1(register_2_q), .in2(register_3_q), .in3(register_4_q), .out(Operator_B),
    .sel(Address_B));
endmodule

module PC (
  input  [7:0] Manual_Address_Innput,
  input  Load,
  input  Clear,
  output [7:0] Address_out
);

  wire clock_1_out;
  wire [7:0] adder_1_out, multiplexer_1_out, multiplexer_2_out;

  Multiplexer #(.width(8), .enable("false")) multiplexer_1 (
    .in0(adder_1_out), .in1(Manual_Address_Innput), .out(multiplexer_1_out), .sel(Load));
  Multiplexer #(.width(8), .enable("false")) multiplexer_2 (
    .in0(8'h1), .in1({8{1'b0}}), .out(multiplexer_2_out), .sel(Load));
  Register register_1 (.D(multiplexer_1_out), .Q(Address_out), .clk(clock_1_out), .clr(Clear));  // open: en
  Clock clock_1 (.out(clock_1_out));
  Adder adder_1 (.a(Address_out), .b(multiplexer_2_out), .out(adder_1_out), .cin(1'b0), .cout(Clear));
endmodule
